// Logisim project Lab3z2.circ as structural Verilog: 1 circuit, main circuit main
module main (
);

  wire ABC_p1, ABC_p2, ABC_p3, nand_1_out, nand_2_out, nand_3_out, nor_1_out, not_1_out, not_2_out, S_out;

  // DipSwitch #(.number(3)) ABC: pin names not known; wires that end beside it: ABC_p1, ABC_p2, ABC_p3
  nor nor_1 (nor_1_out, ABC_p1, ABC_p2, ABC_p3);
  Slider #(.width(1)) S (.out(S_out));
  not not_1 (not_1_out, nor_1_out);
  nand nand_1 (nand_1_out, S_out, not_1_out);
  not not_2 (not_2_out, S_out);
  nand nand_2 (nand_2_out, not_2_out, nor_1_out);
  nand nand_3 (nand_3_out, nand_1_out, nand_2_out);
  LED Y (.in(nand_3_out));

  // Notes on the sheet:
  //   A
  //   B
  //   C
  //   Y = A*!S +B*S
  //   Y = !(!(A*S)*!(B*!S)
endmodule
