// Logisim project Lab3z3.circ as structural Verilog: 1 circuit, main circuit main
module main (
);

  wire and_1_out, and_2_out, not_1_out, or_1_out, slider_1_out;

  Slider #(.width(1)) slider_1 (.out(slider_1_out));
  not not_1 (not_1_out, slider_1_out);
  and and_1 (and_1_out, 1'b1, slider_1_out);
  and and_2 (and_2_out, 1'b1, not_1_out);
  or or_1 (or_1_out, and_1_out, and_2_out);
  LED led_1 (.in(or_1_out));

  // Notes on the sheet:
  //   A
  //   B
  //   S
  //   Y = A*!S +B*S
endmodule
